# Fritzing sketch esp32h2_8relays (saved by Fritzing 1.0.5)
breadboards: 1

parts:
  A1 = esp32-h2 supermini tht

nets:
  N1: A1.Pin_4, A1.Pin_5, A1.Pin_6, A1.Pin_8
  N2: A1.Pin_15, A1.Pin_16, A1.Pin_21

notes:
  5V|3|5|2|1|0|10|11|12|GND

custom parts:
  esp32-h2 supermini tht: esp32-h2 supermini development board.
